# Fritzing sketch ThreeSwitches (saved by Fritzing 0.9.10b)
circuit board: 7cm x 5cm
breadboards: 1

parts:
  Nano = Arduino Nano (Rev3.0)
  +5v- = Screw terminal - 2 pins [package=THT]
  R4 = Resistor [tolerance=±5% power=0.25 resistance=1k package=THT]
  R5 = Resistor [tolerance=±5% power=0.25 resistance=1k package=THT]
  R6 = Resistor [tolerance=±5% power=0.25 resistance=1k package=THT]
  J13 = screw terminal, 3 pins
  Q2 = NPN-Transistor [package="TO92 [THT]"]
  J10 = JST-03JQ-BT [part_number=JST-JQ-BT package=THT]
  RY1 = HF41F relay
  R2 = Resistor [tolerance=±5% power=0.25 resistance=1k package=THT]
  D4 = Rectifier Diode [part_number=1N4001 package="300 mil [THT]"]
  R7 = Resistor [tolerance=±5% power=0.25 resistance=1k package=THT]
  J14 = JST-03JQ-BT [part_number=JST-JQ-BT package=THT]
  Q3 = NPN-Transistor [package="TO92 [THT]"]
  RY2 = HF41F relay
  D5 = Rectifier Diode [part_number=1N4001 package="300 mil [THT]"]
  R8 = Resistor [tolerance=±5% power=0.25 resistance=1k package=THT]
  J15 = JST-03JQ-BT [part_number=JST-JQ-BT package=THT]
  Q4 = NPN-Transistor [package="TO92 [THT]"]
  RY3 = HF41F relay
  D6 = Rectifier Diode [part_number=1N4001 package="300 mil [THT]"]
  J16 = Dagu DGServo 9g header (male) [package=THT]
  J17 = Dagu DGServo 9g header (male) [package=THT]
  J18 = Dagu DGServo 9g header (male) [package=THT]

nets:
  GND: Nano.GND, +5v-.pin1, R4.Pin_1, R5.Pin_1, R6.Pin_1, Q2.E, Q3.E, Q4.E, J16.gnd, J17.gnd, J18.gnd
  N1: Nano.D2, J18.pulse
  N2: Nano.D3, R2.Pin_1
  N3: Nano.D4, R4.Pin_0, J13.pin1
  N4: Nano.D5, J17.pulse
  N5: Nano.D6, R7.Pin_1
  N6: Nano.D7, R5.Pin_0, J13.pin2
  N7: Nano.D8, J16.pulse
  N8: Nano.D9, R8.Pin_1
  N9: Nano.D10, R6.Pin_0, J13.pin3
  VCC: Nano.VIN, +5v-.pin2, RY1.Pin_1, D4.cathode, RY2.Pin_1, D5.cathode, RY3.Pin_1, D6.cathode, J16.Vcc, J17.Vcc, J18.Vcc
  N10: Q2.B, R2.Pin_0
  N11: Q2.C, RY1.Pin_2, D4.anode
  N12: J10.pin2, RY1.Pin_4
  N13: J10.pin1, RY1.Pin_5
  N14: J10.pin3, RY1.Pin_3
  N15: R7.Pin_0, Q3.B
  N16: J14.pin2, RY2.Pin_4
  N17: J14.pin1, RY2.Pin_5
  N18: J14.pin3, RY2.Pin_3
  N19: Q3.C, RY2.Pin_2, D5.anode
  N20: R8.Pin_0, Q4.B
  N21: J15.pin2, RY3.Pin_4
  N22: J15.pin1, RY3.Pin_5
  N23: J15.pin3, RY3.Pin_3
  N24: Q4.C, RY3.Pin_2, D6.anode

custom parts:
  HF41F relay: Subminiature Power Relay 1 form C.
